# Fritzing sketch SRA-scheme (saved by Fritzing 0.9.10b)
breadboards: 2
perfboards: 1

parts:
  Part1 = Arduino Uno (Rev3) - ICSP
  U1 = LCD-16X2 [package=lcd-16x2_nosilk]
  R1 = Resistor [tolerance=±5% resistance=220 package="1206 [SMD]"]
  U2 = POT [knob_status=50% power=0.5W package=alps_pot]
  Mod1 = OLED Mono 0.56 inch blue or white
  T1 = LM35 Temperature Sensor [package="TO92 [THT]"]
  S1 = Momentary Switch [package=ksa_sealed_tac_switch]
  U3 = M10X2 [package=2x10_lock]
  S2 = Momentary Switch [package=ksa_sealed_tac_switch]
  S3 = Momentary Switch [package=ksa_sealed_tac_switch]
  S4 = Momentary Switch [package=ksa_sealed_tac_switch]
  LED1 = smd LED [color="Red (633nm)" package="0805 [SMD]"]
  R2 = Resistor [tolerance=±5% resistance=220 power=0.25 package=THT]
  R3 = Resistor [tolerance=±5% resistance=10k power=0.25 package=THT]
  R4 = Resistor [tolerance=±5% resistance=10k power=0.25 package=THT]
  R5 = Resistor [tolerance=±5% resistance=10k power=0.25 package=THT]
  R6 = Resistor [tolerance=±5% resistance=10k power=0.25 package=THT]
  BULB1 = Incandescent light bulb small [package="bulb sm"]
  Q1 = PNP-Transistor [package="TO92 [THT]"]
  VCC1 = Battery block 9V

nets:
  N1: Part1.A0, T1.Vout
  N2: Part1.ICSP_MISO, Part1.D12/MISO, U3.9
  GND: Part1.GND, U1.VSS, U1.R_W, U1.K, U2.A, Mod1.GND, T1.GND, U3.7
  N3: Part1.D8, U3.15
  N4: Part1.D9_PWM, U3.13
  N5: Part1.D10_PWM/SS, U3.11
  N6: Part1.D11_PWM/MOSI, Q1.B
  N7: Part1.D13/SCK, U3.17
  N8: Part1.A4/SDA, Mod1.SDA
  N9: Part1.A5/SCL, Mod1.SCL
  N10: Part1.D2, U1.DB7
  N11: Part1.D3_PWM, U1.DB6
  N12: Part1.D4, U1.DB5
  N13: Part1.D5_PWM, U1.DB4
  N14: Part1.D6_PWM, U1.RS
  N15: Part1.D7, U1.E
  5V: Part1.5V, U1.VDD, R1.Pin_0, U2.E, Mod1.VCC, T1.+Vs, U3.19
  N16: U1.VO, U2.S
  N17: U1.A, R1.Pin_1
  N18: S1.3, R3.Pin_0
  N19: U3.8, R2.Pin_0
  N20: U3.18, LED1.anode
  N21: U3.20, S4.2
  N22: S2.3, R4.Pin_0
  N23: S3.3, R5.Pin_0
  N24: S4.3, R6.Pin_0
  N25: LED1.cathode, R2.Pin_1
  N26: R3.Pin_1, R4.Pin_1, R6.Pin_1
  N27: BULB1.1, Q1.C
  N28: BULB1.2, VCC1.-
  N29: Q1.E, VCC1.+

custom parts:
  OLED Mono 0.56 inch blue or white: OLED, I2C 3.3V - 5V Blue and White text versions

// code stored in the sketch: Untitled.ino
#include <LiquidCrystal.h>
// Initialize the library with the numbers of the interface pins
LiquidCrystal lcd(6, 7, 5, 4, 3, 2); // RS, E, D4, D5, D6, D7 
void setup() {
// Set up the LCD's number of columns and rows:
lcd.begin(16, 2);
// Print a message to the LCD.
lcd.print("Hello, World!");
}
void loop() {
// Nothing to do here
}
